// Logisim project 2 bit half adder using nand gates.circ as structural Verilog: 1 circuit, main circuit main
module main (
  input  A,
  input  B,
  output SUM,
  output CARRY
);

  wire nand_1_out, nand_2_out, nand_3_out;

  nand nand_1 (nand_1_out, A, B);
  nand nand_2 (nand_2_out, A, nand_1_out);
  nand nand_3 (nand_3_out, nand_1_out, B);
  nand nand_4 (CARRY, nand_1_out, nand_1_out);
  nand nand_5 (SUM, nand_2_out, nand_3_out);
endmodule
